# Fritzing sketch 01_ph4502c_uno (saved by Fritzing 0.9.4b)

parts:
  Arduino_Uno = Arduino Uno (Rev3)
  pH-4502C_+_sonda_BNC = PH meter [package=THT]

nets:
  N1: Arduino_Uno.A0, pH-4502C_+_sonda_BNC.pin1
  N2: Arduino_Uno.5V, pH-4502C_+_sonda_BNC.pin2
  N3: Arduino_Uno.GND, pH-4502C_+_sonda_BNC.pin3
