# Fritzing sketch 01b_ph4502c_esp32 (saved by Fritzing 0.9.4b)
breadboards: 1

parts:
  ESP32_DevKit_V1 = esp32_devkit_v1
  pH-4502C_+_sonda_BNC = PH meter [package=THT]
  1_kΩ = Resistor [resistance=1k package=THT]
  2_kΩ = Resistor [resistance=2k package=THT]

nets:
  N1: ESP32_DevKit_V1.connector1, pH-4502C_+_sonda_BNC.pin3, 2_kΩ.Pin_1
  N2: ESP32_DevKit_V1.connector18, 1_kΩ.Pin_1, 2_kΩ.Pin_0
  N3: ESP32_DevKit_V1.connector29, pH-4502C_+_sonda_BNC.pin2
  N4: pH-4502C_+_sonda_BNC.pin1, 1_kΩ.Pin_0
