# Fritzing sketch 02_yfs201_uno (saved by Fritzing 0.9.4b)
breadboards: 1

parts:
  Arduino_Uno = Arduino Uno (Rev3)
  YF-S201 = cria_yfs201

nets:
  N1: Arduino_Uno.D2, YF-S201.connector1
  N2: Arduino_Uno.5V, YF-S201.connector0
  N3: Arduino_Uno.GND, YF-S201.connector2
