# Fritzing sketch 03_hx710b_uno (saved by Fritzing 0.9.4b)
breadboards: 1

parts:
  Arduino_Uno = Arduino Uno (Rev3)
  HX710B = cria_hx710b

nets:
  N1: Arduino_Uno.D3_PWM, HX710B.connector1
  N2: Arduino_Uno.D4, HX710B.connector2
  N3: Arduino_Uno.5V, HX710B.connector0
  N4: Arduino_Uno.GND, HX710B.connector3
