# Fritzing sketch 04_monitor_agua_uno (saved by Fritzing 0.9.4b)
breadboards: 1

parts:
  Arduino_Uno = Arduino Uno (Rev3)
  YF-S201 = cria_yfs201
  HX710B = cria_hx710b
  LED_RGB = RGB LED (com. cathode, rgb) [package="5 mm [THT]"]
  220_Ω = Resistor [resistance=220 package=THT]
  220_Ω_2 = Resistor [resistance=220 package=THT]
  220_Ω_3 = Resistor [resistance=220 package=THT]
  Buzzer = Buzzer 12mm [package=buzzer-12mm-ns]
  pH-4502C_+_sonda_BNC = PH meter [package=THT]

nets:
  N1: Arduino_Uno.A0, pH-4502C_+_sonda_BNC.pin1
  N2: Arduino_Uno.D8, Buzzer.1
  N3: Arduino_Uno.D9_PWM, 220_Ω.Pin_1
  N4: Arduino_Uno.D2, YF-S201.connector1
  N5: Arduino_Uno.D3_PWM, HX710B.connector1
  N6: Arduino_Uno.D4, HX710B.connector2
  N7: Arduino_Uno.D5_PWM, 220_Ω_3.Pin_1
  N8: Arduino_Uno.D6_PWM, 220_Ω_2.Pin_1
  N9: Arduino_Uno.5V, YF-S201.connector0, HX710B.connector0, pH-4502C_+_sonda_BNC.pin2
  N10: Arduino_Uno.GND, YF-S201.connector2, HX710B.connector3, LED_RGB.common_cathode, Buzzer.2, pH-4502C_+_sonda_BNC.pin3
  N11: LED_RGB.red_anode, 220_Ω.Pin_0
  N12: LED_RGB.green_anode, 220_Ω_2.Pin_0
  N13: LED_RGB.blue_anode, 220_Ω_3.Pin_0
