# Fritzing sketch 04b_monitor_agua_esp32 (saved by Fritzing 0.9.4b)
breadboards: 1

parts:
  ESP32_DevKit_V1 = esp32_devkit_v1
  YF-S201 = cria_yfs201
  1_kΩ = Resistor [resistance=1k package=THT]
  2_kΩ = Resistor [resistance=2k package=THT]
  HX710B = cria_hx710b
  LED_RGB = RGB LED (com. cathode, rgb) [package="5 mm [THT]"]
  220_Ω = Resistor [resistance=220 package=THT]
  220_Ω_2 = Resistor [resistance=220 package=THT]
  220_Ω_3 = Resistor [resistance=220 package=THT]
  Buzzer = Buzzer 12mm [package=buzzer-12mm-ns]
  pH-4502C_+_sonda_BNC = PH meter [package=THT]
  1_kΩ_2 = Resistor [resistance=1k package=THT]
  2_kΩ_2 = Resistor [resistance=2k package=THT]

nets:
  N1: ESP32_DevKit_V1.connector0, HX710B.connector0
  N2: ESP32_DevKit_V1.connector1, YF-S201.connector2, 2_kΩ.Pin_1, HX710B.connector3, LED_RGB.common_cathode, Buzzer.2, pH-4502C_+_sonda_BNC.pin3, 2_kΩ_2.Pin_1
  N3: ESP32_DevKit_V1.connector8, HX710B.connector1
  N4: ESP32_DevKit_V1.connector9, HX710B.connector2
  N5: ESP32_DevKit_V1.connector18, 1_kΩ_2.Pin_1, 2_kΩ_2.Pin_0
  N6: ESP32_DevKit_V1.connector21, 220_Ω_3.Pin_1
  N7: ESP32_DevKit_V1.connector22, 220_Ω.Pin_1
  N8: ESP32_DevKit_V1.connector23, 220_Ω_2.Pin_1
  N9: ESP32_DevKit_V1.connector24, 1_kΩ.Pin_1, 2_kΩ.Pin_0
  N10: ESP32_DevKit_V1.connector25, Buzzer.1
  N11: ESP32_DevKit_V1.connector29, YF-S201.connector0, pH-4502C_+_sonda_BNC.pin2
  N12: YF-S201.connector1, 1_kΩ.Pin_0
  N13: LED_RGB.red_anode, 220_Ω.Pin_0
  N14: LED_RGB.green_anode, 220_Ω_2.Pin_0
  N15: LED_RGB.blue_anode, 220_Ω_3.Pin_0
  N16: pH-4502C_+_sonda_BNC.pin1, 1_kΩ_2.Pin_0
