# Fritzing sketch 01_dht11_uno (saved by Fritzing 0.9.4b)
breadboards: 1

parts:
  Arduino_Uno = Arduino Uno (Rev3)
  DHT11_(módulo_3_pinos) = cria_dht11_mod3

nets:
  N1: Arduino_Uno.D2, DHT11_(módulo_3_pinos).connector1
  N2: Arduino_Uno.5V, DHT11_(módulo_3_pinos).connector0
  N3: Arduino_Uno.GND, DHT11_(módulo_3_pinos).connector2
