# Fritzing sketch 02_dht22_uno (saved by Fritzing 0.9.4b)
breadboards: 1

parts:
  Arduino_Uno = Arduino Uno (Rev3)
  DHT22_(3_fios) = cria_dht22_fios

nets:
  N1: Arduino_Uno.D2, DHT22_(3_fios).connector1
  N2: Arduino_Uno.5V, DHT22_(3_fios).connector0
  N3: Arduino_Uno.GND, DHT22_(3_fios).connector2
