# Fritzing sketch 03_mq2_uno (saved by Fritzing 0.9.4b)
breadboards: 1

parts:
  Arduino_Uno = Arduino Uno (Rev3)
  MQ-2 = mq_modulo

nets:
  N1: Arduino_Uno.A0, MQ-2.connector3
  N2: Arduino_Uno.D3_PWM, MQ-2.connector2
  N3: Arduino_Uno.5V, MQ-2.connector0
  N4: Arduino_Uno.GND, MQ-2.connector1
