# Fritzing sketch 05_mhz19b_uno (saved by Fritzing 0.9.4b)
breadboards: 1

parts:
  Arduino_Uno = Arduino Uno (Rev3)
  MH-Z19B = cria_mhz19b
  1_kΩ = Resistor [resistance=1k package=THT]
  2_kΩ = Resistor [resistance=2k package=THT]

nets:
  N1: Arduino_Uno.D10_PWM/SS, MH-Z19B.connector3
  N2: Arduino_Uno.D11_PWM/MOSI, 1_kΩ.Pin_1
  N3: Arduino_Uno.5V, MH-Z19B.connector0
  N4: Arduino_Uno.GND, MH-Z19B.connector1, 2_kΩ.Pin_0
  N5: MH-Z19B.connector2, 1_kΩ.Pin_0, 2_kΩ.Pin_1
