# Fritzing sketch 05_mhz19c_uno (saved by Fritzing 0.9.4b)
breadboards: 1

parts:
  Arduino_Uno = Arduino Uno (Rev3)
  MH-Z19C = cria_mhz19c
  1_kΩ = Resistor [resistance=1k package=THT]
  2_kΩ = Resistor [resistance=2k package=THT]

nets:
  N1: Arduino_Uno.D10_PWM/SS, MH-Z19C.connector2
  N2: Arduino_Uno.D11_PWM/MOSI, 1_kΩ.Pin_1, 2_kΩ.Pin_0
  N3: Arduino_Uno.5V, MH-Z19C.connector8
  N4: Arduino_Uno.GND, MH-Z19C.connector7, 2_kΩ.Pin_1
  N5: MH-Z19C.connector3, 1_kΩ.Pin_0
