# Fritzing sketch 06_monitor_ar_uno (saved by Fritzing 0.9.4b)
breadboards: 1

parts:
  Arduino_Uno = Arduino Uno (Rev3)
  DHT11 = cria_dht11_mod3
  DHT22 = cria_dht22_fios
  MQ-2 = mq_modulo
  MQ-135 = mq_modulo
  MH-Z19C = cria_mhz19c
  1_kΩ = Resistor [resistance=1k package=THT]
  2_kΩ = Resistor [resistance=2k package=THT]
  LED_RGB = RGB LED (com. cathode, rgb) [package="5 mm [THT]"]
  220_Ω = Resistor [resistance=220 package=THT]
  220_Ω_2 = Resistor [resistance=220 package=THT]
  220_Ω_3 = Resistor [resistance=220 package=THT]

nets:
  N1: Arduino_Uno.A0, MQ-2.connector3
  N2: Arduino_Uno.A1, MQ-135.connector3
  N3: Arduino_Uno.D9_PWM, 220_Ω.Pin_1
  N4: Arduino_Uno.D10_PWM/SS, MH-Z19C.connector2
  N5: Arduino_Uno.D11_PWM/MOSI, 1_kΩ.Pin_1, 2_kΩ.Pin_0
  N6: Arduino_Uno.D2, DHT11.connector1
  N7: Arduino_Uno.D4, DHT22.connector1
  N8: Arduino_Uno.D5_PWM, 220_Ω_3.Pin_1
  N9: Arduino_Uno.D6_PWM, 220_Ω_2.Pin_1
  N10: Arduino_Uno.5V, DHT11.connector0, DHT22.connector0, MQ-2.connector0, MQ-135.connector0, MH-Z19C.connector8
  N11: Arduino_Uno.GND, DHT11.connector2, DHT22.connector2, MQ-2.connector1, MQ-135.connector1, MH-Z19C.connector7, 2_kΩ.Pin_1, LED_RGB.common_cathode
  N12: MH-Z19C.connector3, 1_kΩ.Pin_0
  N13: LED_RGB.red_anode, 220_Ω.Pin_0
  N14: LED_RGB.green_anode, 220_Ω_2.Pin_0
  N15: LED_RGB.blue_anode, 220_Ω_3.Pin_0
