# Fritzing sketch 01_uno_hcsr04 (saved by Fritzing 0.9.4b)
breadboards: 1

parts:
  Arduino_Uno = Arduino Uno (Rev3)
  HC-SR04 = HC-SR04 Ultrasonic Distance Sensor

nets:
  N1: Arduino_Uno.D9_PWM, HC-SR04.TRIG
  N2: Arduino_Uno.D10_PWM/SS, HC-SR04.ECHO
  5V: Arduino_Uno.5V, HC-SR04.VCC
  GND: Arduino_Uno.GND, HC-SR04.GND
