# Fritzing sketch 02_uno_buzzer (saved by Fritzing 0.9.4b)
breadboards: 1

parts:
  Arduino_Uno = Arduino Uno (Rev3)
  Buzzer = Buzzer 12mm [package=buzzer-12mm-ns]

nets:
  N1: Arduino_Uno.D8, Buzzer.1
  N2: Arduino_Uno.GND, Buzzer.2
