# Fritzing sketch 03_uno_alarme_re (saved by Fritzing 0.9.4b)
breadboards: 1

parts:
  Arduino_Uno = Arduino Uno (Rev3)
  HC-SR04 = HC-SR04 Ultrasonic Distance Sensor
  LED_RGB = RGB LED (com. cathode, rgb) [package="5 mm [THT]"]
  220_Ω = Resistor [resistance=220 package=THT]
  220_Ω_2 = Resistor [resistance=220 package=THT]
  220_Ω_3 = Resistor [resistance=220 package=THT]
  Buzzer = Buzzer 12mm [package=buzzer-12mm-ns]

nets:
  N1: Arduino_Uno.D8, Buzzer.1
  N2: Arduino_Uno.D9_PWM, HC-SR04.TRIG
  N3: Arduino_Uno.D10_PWM/SS, HC-SR04.ECHO
  N4: Arduino_Uno.D3_PWM, 220_Ω_3.Pin_1
  N5: Arduino_Uno.D5_PWM, 220_Ω.Pin_1
  N6: Arduino_Uno.D6_PWM, 220_Ω_2.Pin_1
  5V: Arduino_Uno.5V, HC-SR04.VCC
  GND: Arduino_Uno.GND, HC-SR04.GND, LED_RGB.common_cathode, Buzzer.2
  N7: LED_RGB.red_anode, 220_Ω.Pin_0
  N8: LED_RGB.green_anode, 220_Ω_2.Pin_0
  N9: LED_RGB.blue_anode, 220_Ω_3.Pin_0
