# Fritzing sketch 03_gestos_rgb (saved by Fritzing 0.9.4b)
breadboards: 1

parts:
  ESP32-CAM = esp32cam
  LED_RGB = RGB LED (com. cathode, rgb) [package="5 mm [THT]"]
  220_Ω = Resistor [resistance=220 package=THT]
  220_Ω_2 = Resistor [resistance=220 package=THT]
  220_Ω_3 = Resistor [resistance=220 package=THT]

nets:
  N1: ESP32-CAM.connector1, LED_RGB.common_cathode
  N2: ESP32-CAM.connector2, 220_Ω.Pin_1
  N3: ESP32-CAM.connector3, 220_Ω_2.Pin_1
  N4: ESP32-CAM.connector5, 220_Ω_3.Pin_1
  N5: LED_RGB.red_anode, 220_Ω.Pin_0
  N6: LED_RGB.green_anode, 220_Ω_2.Pin_0
  N7: LED_RGB.blue_anode, 220_Ω_3.Pin_0
