# Fritzing sketch 01_uno_led (saved by Fritzing 0.9.4b)
breadboards: 1

parts:
  Arduino_Uno = Arduino Uno (Rev3)
  LED = LED - 5mm [color="Red (633nm)" package="5 mm [THT]"]
  220_Ω = Resistor [resistance=220 package=THT]

nets:
  N1: Arduino_Uno.D8, 220_Ω.Pin_1
  N2: Arduino_Uno.GND, LED.cathode
  N3: LED.anode, 220_Ω.Pin_0
