# Fritzing sketch 02_uno_led_botao (saved by Fritzing 0.9.4b)
breadboards: 1

parts:
  Arduino_Uno = Arduino Uno (Rev3)
  LED = LED - 5mm [color="Red (633nm)" package="5 mm [THT]"]
  220_Ω = Resistor [resistance=220 package=THT]
  Botão = Round Pushbutton

nets:
  N1: Arduino_Uno.D8, 220_Ω.Pin_1
  N2: Arduino_Uno.D2, Botão.leg0
  N3: Arduino_Uno.GND, LED.cathode, Botão.leg1
  N4: LED.anode, 220_Ω.Pin_0
