# Fritzing sketch 04_uno_semaforo_botao (saved by Fritzing 0.9.4b)
breadboards: 1

parts:
  Arduino_Uno = Arduino Uno (Rev3)
  LED_vermelho = LED - 5mm [color="Red (633nm)" package="5 mm [THT]"]
  220_Ω = Resistor [resistance=220 package=THT]
  LED_amarelo = LED - 5mm [color="Yellow (595nm)" package="5 mm [THT]"]
  220_Ω_2 = Resistor [resistance=220 package=THT]
  LED_verde = LED - 5mm [color="Green (570nm)" package="5 mm [THT]"]
  220_Ω_3 = Resistor [resistance=220 package=THT]
  Botão_pedestre = Round Pushbutton

nets:
  N1: Arduino_Uno.D8, 220_Ω_3.Pin_1
  N2: Arduino_Uno.D9_PWM, 220_Ω_2.Pin_1
  N3: Arduino_Uno.D10_PWM/SS, 220_Ω.Pin_1
  N4: Arduino_Uno.D2, Botão_pedestre.leg0
  N5: Arduino_Uno.GND, LED_vermelho.cathode, LED_amarelo.cathode, LED_verde.cathode, Botão_pedestre.leg1
  N6: LED_vermelho.anode, 220_Ω.Pin_0
  N7: LED_amarelo.anode, 220_Ω_2.Pin_0
  N8: LED_verde.anode, 220_Ω_3.Pin_0
