# Fritzing sketch 05_uno_rgb_pot (saved by Fritzing 0.9.4b)
breadboards: 1

parts:
  Arduino_Uno = Arduino Uno (Rev3)
  LED_RGB = RGB LED (com. cathode, rgb) [package="5 mm [THT]"]
  220_Ω = Resistor [resistance=220 package=THT]
  220_Ω_2 = Resistor [resistance=220 package=THT]
  220_Ω_3 = Resistor [resistance=220 package=THT]
  Pot_10k = Rotary Potentiometer (Large) [package=THT]
  Botão_modo = Round Pushbutton

nets:
  N1: Arduino_Uno.A0, Pot_10k.wiper
  N2: Arduino_Uno.D9_PWM, 220_Ω.Pin_1
  N3: Arduino_Uno.D10_PWM/SS, 220_Ω_2.Pin_1
  N4: Arduino_Uno.D11_PWM/MOSI, 220_Ω_3.Pin_1
  N5: Arduino_Uno.D2, Botão_modo.leg0
  N6: Arduino_Uno.5V, Pot_10k.leg2
  N7: Arduino_Uno.GND, LED_RGB.common_cathode, Pot_10k.leg1, Botão_modo.leg1
  N8: LED_RGB.red_anode, 220_Ω.Pin_0
  N9: LED_RGB.green_anode, 220_Ω_2.Pin_0
  N10: LED_RGB.blue_anode, 220_Ω_3.Pin_0
