# Fritzing sketch 01_ds18b20_uno (saved by Fritzing 0.9.4b)
breadboards: 1

parts:
  Arduino_Uno = Arduino Uno (Rev3)
  DS18B20 = DS18B20 1-Wire Temperature Sensor
  4_7_kΩ = Resistor [resistance=4.7k package=THT]

nets:
  N1: Arduino_Uno.D2, DS18B20.DQ, 4_7_kΩ.Pin_0
  5V: Arduino_Uno.5V, DS18B20.VDD, 4_7_kΩ.Pin_1
  GND: Arduino_Uno.GND, DS18B20.GND
