# Fritzing sketch 01b_ds18b20_esp32 (saved by Fritzing 0.9.4b)
breadboards: 1

parts:
  ESP32_DevKit_V1 = esp32_devkit_v1
  DS18B20 = DS18B20 1-Wire Temperature Sensor
  4_7_kΩ = Resistor [resistance=4.7k package=THT]

nets:
  N1: ESP32_DevKit_V1.connector0, DS18B20.VDD, 4_7_kΩ.Pin_1
  N2: ESP32_DevKit_V1.connector1, DS18B20.GND
  N3: ESP32_DevKit_V1.connector4, DS18B20.DQ, 4_7_kΩ.Pin_0
