# Fritzing sketch 02_dht11_uno (saved by Fritzing 0.9.4b)
breadboards: 1

parts:
  Arduino_Uno = Arduino Uno (Rev3)
  DHT11 = dht11
  10_kΩ = Resistor [resistance=10k package=THT]

nets:
  N1: Arduino_Uno.D2, DHT11.connector2, 10_kΩ.Pin_0
  N2: Arduino_Uno.5V, DHT11.connector1, 10_kΩ.Pin_1
  N3: Arduino_Uno.GND, DHT11.connector4
