# Fritzing sketch 04_mq135_uno (saved by Fritzing 0.9.4b)
breadboards: 1

parts:
  Arduino_Uno = Arduino Uno (Rev3)
  MQ-135 = mq_modulo

nets:
  N1: Arduino_Uno.A0, MQ-135.connector3
  N2: Arduino_Uno.D3_PWM, MQ-135.connector2
  N3: Arduino_Uno.5V, MQ-135.connector0
  N4: Arduino_Uno.GND, MQ-135.connector1
