# Fritzing sketch 05_bme680_uno (saved by Fritzing 0.9.4b)
breadboards: 1

parts:
  Arduino_Uno = Arduino Uno (Rev3)
  BME680 = bme680

nets:
  N1: Arduino_Uno.A4/SDA, BME680.connector42
  N2: Arduino_Uno.A5/SCL, BME680.connector40
  N3: Arduino_Uno.5V, BME680.connector37
  N4: Arduino_Uno.GND, BME680.connector39
