# Fritzing sketch 01_uno_servo (saved by Fritzing 0.9.4b)

parts:
  Arduino_Uno = Arduino Uno (Rev3)
  Servo_SG90 = Basic Servo

nets:
  N1: Arduino_Uno.D9_PWM, Servo_SG90.pulse
  5V: Arduino_Uno.5V, Servo_SG90.vcc
  GND: Arduino_Uno.GND, Servo_SG90.gnd
