# Fritzing sketch 02_uno_pot_servo (saved by Fritzing 0.9.4b)
breadboards: 1

parts:
  Arduino_Uno = Arduino Uno (Rev3)
  Pot_10k = Rotary Potentiometer (Large) [package=THT]
  Servo_SG90 = Basic Servo

nets:
  N1: Arduino_Uno.A0, Pot_10k.wiper
  N2: Arduino_Uno.D9_PWM, Servo_SG90.pulse
  5V: Arduino_Uno.5V, Pot_10k.leg2, Servo_SG90.vcc
  GND: Arduino_Uno.GND, Pot_10k.leg1, Servo_SG90.gnd
